// Logisim project Ammar --Final.circ as structural Verilog: 7 circuits, main circuit Main
module Main (
  input  Reset,
  input  Enable,
  output c1,
  output c0,
  output not_found,
  output found
);

  wire and_1_out, and_2_out, and_4_out, Clock_out, expected_output_1_out_5, n4_input_validate_1_v,
       n4_output_test_ic_1_ic0, n4_output_test_ic_1_ic1, n4_output_test_ic_1_ic2, n4_output_test_ic_1_ic3,
       n74ls161_4_bit_counter_1_q0, n74ls161_4_bit_counter_1_q1, not_1_out, not_2_out, optimise_counter_1_e,
       optimise_counter_1_l, xor_1_out;

  Clock Clock (.out(Clock_out));
  and and_1 (and_1_out, Enable, optimise_counter_1_e);
  _74LS161_4_bit_counter u_74ls161_4_bit_counter_1 (
    .L3(xor_1_out), .L2(not_2_out), .L1(1'b0), .L0(1'b0), .ENP(and_1_out), .ENT(and_1_out), .CLK(Clock_out),
    .nCLR(Reset), .nLOAD(not_1_out), .Q3(c1), .Q2(c0), .Q1(n74ls161_4_bit_counter_1_q1),
    .Q0(n74ls161_4_bit_counter_1_q0));  // open: RCO
  not not_1 (not_1_out, and_2_out);
  and and_2 (and_2_out, Enable, optimise_counter_1_l);
  not not_2 (not_2_out, c0);
  Expected_Output expected_output_1 (
    .Test_Case_0(n74ls161_4_bit_counter_1_q1), .Test_Case_1(n74ls161_4_bit_counter_1_q0), .IC_Type_1(c1),
    .IC_Type_0(c0), .out_5(expected_output_1_out_5));
  xor xor_1 (xor_1_out, c0, c1);
  Optimise_Counter optimise_counter_1 (
    .nf(not_found), .v(n4_input_validate_1_v), .c3(c1), .nc2(not_2_out), .e(optimise_counter_1_e),
    .L(optimise_counter_1_l));
  _4_output_Test_IC u_4_output_test_ic_1 (
    .A(n74ls161_4_bit_counter_1_q1), .B(n74ls161_4_bit_counter_1_q0), .IC0(n4_output_test_ic_1_ic0),
    .IC1(n4_output_test_ic_1_ic1), .IC2(n4_output_test_ic_1_ic2), .IC3(n4_output_test_ic_1_ic3));
  _4_Input_Validate u_4_input_validate_1 (
    .e(expected_output_1_out_5), .IC0(n4_output_test_ic_1_ic0), .IC1(n4_output_test_ic_1_ic1),
    .IC2(n4_output_test_ic_1_ic2), .IC3(n4_output_test_ic_1_ic3), .V(n4_input_validate_1_v));
  and and_3 (found, n4_input_validate_1_v, and_4_out);
  not not_3 (not_found, found);
  and and_4 (and_4_out, n74ls161_4_bit_counter_1_q0, n74ls161_4_bit_counter_1_q1);
endmodule

module Expected_Output (
  input  Test_Case_0,
  input  Test_Case_1,
  input  IC_Type_1,
  input  IC_Type_0,
  output out_5
);

  wire and_1_out, nand_1_out, or_1_out, xor_1_out;

  or or_1 (or_1_out, Test_Case_0, Test_Case_1);
  xor xor_1 (xor_1_out, Test_Case_0, Test_Case_1);
  nand nand_1 (nand_1_out, Test_Case_0, Test_Case_1);
  and and_1 (and_1_out, Test_Case_0, Test_Case_1);
  Multiplexer #(.select(2)) multiplexer_1 (
    .in0(and_1_out), .in1(or_1_out), .in2(xor_1_out), .in3(nand_1_out), .out(out_5),
    .sel({IC_Type_1, IC_Type_0}));  // open: en
endmodule

// Validate
module _4_Input_Validate (
  input  e,
  input  IC0,
  input  IC1,
  input  IC2,
  input  IC3,
  output V
);

  wire and_1_out, and_2_out, xnor_1_out, xnor_2_out, xnor_3_out, xnor_4_out;

  xnor xnor_1 (xnor_1_out, e, IC0);
  xnor xnor_2 (xnor_2_out, e, IC1);
  xnor xnor_3 (xnor_3_out, e, IC2);
  xnor xnor_4 (xnor_4_out, e, IC3);
  and and_1 (and_1_out, xnor_1_out, xnor_2_out);
  and and_2 (and_2_out, xnor_3_out, xnor_4_out);
  and and_3 (V, and_1_out, and_2_out);
endmodule

// Test IC
module _4_output_Test_IC (
  input  A,
  input  B,
  output IC0,
  output IC1,
  output IC2,
  output IC3
);

  // XNOR_Gate xnor_1 is placed but not wired
  // XNOR_Gate xnor_2 is placed but not wired
  // XNOR_Gate xnor_3 is placed but not wired
  // XNOR_Gate xnor_4 is placed but not wired
  // NOR_Gate nor_1 is placed but not wired
  // NOR_Gate nor_2 is placed but not wired
  // NOR_Gate nor_3 is placed but not wired
  // NOR_Gate nor_4 is placed but not wired
  and and_1 (IC0, A, B);
  and and_2 (IC1, A, B);
  and and_3 (IC2, A, B);
  and and_4 (IC3, A, B);
  // XOR_Gate xor_1 is placed but not wired
  // XOR_Gate xor_2 is placed but not wired
  // XOR_Gate xor_3 is placed but not wired
  // XOR_Gate xor_4 is placed but not wired
  // OR_Gate or_1 is placed but not wired
  // OR_Gate or_2 is placed but not wired
  // OR_Gate or_3 is placed but not wired
  // OR_Gate or_4 is placed but not wired
  // NAND_Gate nand_1 is placed but not wired
  // NAND_Gate nand_2 is placed but not wired
  // NAND_Gate nand_3 is placed but not wired
  // NAND_Gate nand_4 is placed but not wired
  // AND_Gate and_5 is placed but not wired
  // AND_Gate and_6 is placed but not wired
  // AND_Gate and_7 is placed but not wired
  // AND_Gate and_8 is placed but not wired

  // Notes on the sheet:
  //   invalid
  //   valid
endmodule

module Optimise_Counter (
  input  nf,
  input  v,
  input  c3,
  input  nc2,
  output L,
  output e
);

  wire not_1_out, not_2_out, or_1_out;

  not not_1 (not_1_out, c3);
  or or_1 (or_1_out, not_1_out, nc2);
  not not_2 (not_2_out, v);
  and and_1 (e, nf, v);
  and and_2 (L, or_1_out, not_2_out);
endmodule

module _74LS161_4_bit_counter (
  input  L3,
  input  L2,
  input  L1,
  input  L0,
  input  ENP,
  input  ENT,
  input  nLOAD,
  input  nCLR,
  input  CLK,
  output Q3,
  output Q2,
  output Q1,
  output Q0,
  output RCO
);

  wire and_1_out, and_2_out, not_1_out, not_2_out;

  and and_1 (and_1_out, ENP, ENT);
  and and_2 (and_2_out, and_1_out, nLOAD);
  not not_1 (not_1_out, nLOAD);
  not not_2 (not_2_out, nCLR);
  Counter #(.width(4), .max('hf)) counter_1 (
    .load(not_1_out), .D({L3, L2, L1, L0}), .count(and_2_out), .Q({Q3, Q2, Q1, Q0}), .carry(RCO), .clk(CLK),
    .clr(not_2_out));
endmodule

module _2_4_MUX (
  input  C0,
  input  C1,
  input  I0,
  input  I1,
  input  I2,
  input  I3,
  output O
);

  wire and_1_out, and_2_out, and_3_out, and_4_out, not_1_out, not_2_out, not_3_out, not_4_out;

  not not_1 (not_1_out, C0);
  not not_2 (not_2_out, C1);
  not not_3 (not_3_out, C0);
  not not_4 (not_4_out, C1);
  and and_1 (and_1_out, not_1_out, not_2_out, I0);
  and and_2 (and_2_out, not_3_out, C1, I1);
  and and_3 (and_3_out, C0, not_4_out, I2);
  and and_4 (and_4_out, C0, C1, I3);
  or or_1 (O, and_1_out, and_2_out, and_3_out, and_4_out);
endmodule
